# Fritzing sketch Project1 (saved by Fritzing 0.9.3b)
breadboards: 1

parts:
  Power_plug_(3_8v_to_4_2v) = Power plug
  GSM_SIM_GPSR_SMS_SIM900_SIM1 = SIM800L [package=THT]
  Part1 = Arduino Uno (Rev3)
  U1 = LCD-16X2 [package=lcd-8x2]
  R3 = Resistor [tolerance=±5% resistance=220 package=THT]
  R4 = Trimmer Potentiometer [maximum_resistance=10kΩ package=THT]
  Signal_Input_From_Energy_Meter = mystery part, 1 pin [chip_label=?]

nets:
  VCC: Power_plug_(3_8v_to_4_2v).VCC, GSM_SIM_GPSR_SMS_SIM900_SIM1.5V
  GND: Power_plug_(3_8v_to_4_2v).GND, GSM_SIM_GPSR_SMS_SIM900_SIM1.GND, Part1.GND, U1.VSS, R4.leg1
  N1: GSM_SIM_GPSR_SMS_SIM900_SIM1.SIM_TXD, Part1.D10_PWM/SS
  N2: GSM_SIM_GPSR_SMS_SIM900_SIM1.SIM_RXD, Part1.D11_PWM/MOSI
  N3: Part1.A0, Signal_Input_From_Energy_Meter.pin1
  N4: Part1.D8, U1.RS
  N5: Part1.D3_PWM, U1.DB7
  N6: Part1.D4, U1.DB6
  N7: Part1.D5_PWM, U1.DB5
  N8: Part1.D6_PWM, U1.DB4
  N9: Part1.D7, U1.E
  5V: Part1.5V, U1.VDD, U1.R_W, R3.Pin_0, R4.leg2
  N10: U1.VO, R4.wiper
  N11: U1.A, R3.Pin_1
